// Logisim project processor.circ as structural Verilog: 2 circuits, main circuit ALU
module ALU (
  input  [15:0] A,
  input  [15:0] B,
  input  [3:0] OP,
  output [15:0] out_4
);

  wire [15:0] adder_1_out, and_1_out, divider_1_out, multiplier_1_out, nand_1_out, nor_1_out, not_1_out,
       or_1_out, shifter_1_out, shifter_2_out, subtractor_1_out, xor_1_out;

  Adder #(.width(16)) adder_1 (.a(A), .b(B), .out(adder_1_out));  // open: cin, cout
  Subtractor #(.width(16)) subtractor_1 (.a(A), .b(B), .out(subtractor_1_out));  // open: bin, bout
  Multiplier #(.width(16)) multiplier_1 (.a(A), .b(B), .out(multiplier_1_out));  // open: cin, cout
  Shifter #(.shift("lr"), .width(16)) shifter_1 (.in(A), .\dist (B[3:0]), .out(shifter_1_out));
  Divider #(.width(16)) divider_1 (.a(A), .b(B), .out(divider_1_out));  // open: upper, rem
  Shifter #(.width(16)) shifter_2 (.in(A), .\dist (B[3:0]), .out(shifter_2_out));
  assign not_1_out = ~A;  // NOT_Gate not_1, 16 bits wide
  assign and_1_out = A & B;  // AND_Gate and_1, 16 bits wide
  assign or_1_out = A | B;  // OR_Gate or_1, 16 bits wide
  assign xor_1_out = A ^ B;  // XOR_Gate xor_1, 16 bits wide
  assign nor_1_out = ~(A | B);  // NOR_Gate nor_1, 16 bits wide
  assign nand_1_out = ~(A & B);  // NAND_Gate nand_1, 16 bits wide
  Multiplexer #(.select(4), .width(16)) multiplexer_1 (
    .in0(adder_1_out), .in1(subtractor_1_out), .in2(multiplier_1_out), .in3(shifter_1_out),
    .in4(divider_1_out), .in5(shifter_2_out), .in6(not_1_out), .in7(and_1_out), .in8(or_1_out),
    .in9(nand_1_out), .in10(xor_1_out), .in11(nor_1_out), .in12({16{1'b0}}), .in13({16{1'b0}}),
    .in14({16{1'b0}}), .in15({16{1'b0}}), .out(out_4), .sel(OP));
endmodule

module CPU (
  output [15:0] out_1,
  output [4:0] out_2,
  output [10:0] out_3,
  output [2:0] dest,
  output [2:0] src,
  output [15:0] out_6
);

  wire ALUen, button_1_out, clk, comparator_2_gt, comparator_3_lt, demultiplexer_1_out0,
       demultiplexer_1_out1, demultiplexer_1_out2, demultiplexer_1_out3, demultiplexer_1_out4,
       demultiplexer_1_out5, demultiplexer_1_out6, demultiplexer_1_out7, loadIm, mv, or_5_out, register_3_q,
       rst;
  wire [2:0] a, a1, a2, multiplexer_4_out, multiplexer_5_out, multiplexer_6_out, multiplexer_7_out;
  wire [3:0] bit_extender_2_out;
  wire [4:0] subtractor_1_out;
  wire [7:0] PC_q;
  wire [15:0] ALUdata, demultiplexer_2_out0, demultiplexer_2_out1, demultiplexer_2_out2,
       demultiplexer_2_out3, demultiplexer_2_out4, demultiplexer_2_out5, demultiplexer_2_out6,
       demultiplexer_2_out7, imVal, multiplexer_1_out, multiplexer_2_out, multiplexer_3_out, or_1_out, out1,
       out2, R0_q, R1_q, R2_q, R3_q, R4_q, R5_q, R6_q, R7_q, register_1_q;

  Clock clock_1 (.out(clk));
  Counter PC (.Q(PC_q), .clk(clk), .clr(button_1_out));  // open: load, D, count, carry, up
  Button button_1 (.out(button_1_out));
  Button Reset (.out(rst));
  ROM #(.dataWidth(16)) rom_1 (.addr(PC_q), .data({out_1[15:8], dest, out_1[4:0]}));
  Comparator #(.mode("unsigned"), .width(5)) comparator_1 (
    .a(out_1[15:11]), .b(5'b10010), .eq(loadIm));  // open: gt, lt
  assign imVal = {{8{dest[2]}}, {dest, out_1[4:0]}};  // Bit_Extender bit_extender_1
  Comparator #(.width(5)) comparator_2 (.a(out_1[15:11]), .b(5'b00010), .gt(comparator_2_gt));  // open: eq, lt
  Comparator #(.width(5)) comparator_3 (.a(out_1[15:11]), .b(5'b01111), .lt(comparator_3_lt));  // open: gt, eq
  and and_1 (ALUen, comparator_2_gt, comparator_3_lt);
  Comparator #(.mode("unsigned"), .width(5)) comparator_4 (.a(out_1[15:11]), .b(5'b10011), .eq(mv));  // open: gt, lt
  Register #(.width(16)) register_1 (.D(out1), .en(mv), .Q(register_1_q), .clk(clk), .clr(rst));
  Subtractor #(.width(5)) subtractor_1 (.a(out_1[15:11]), .b(5'b00011), .out(subtractor_1_out));  // open: bin, bout
  Multiplexer #(.width(16)) multiplexer_1 (.in0({16{1'b0}}), .in1(register_1_q), .out(multiplexer_1_out), .sel(mv));
  Multiplexer #(.width(16)) multiplexer_2 (.in0({16{1'b0}}), .in1(imVal), .out(multiplexer_2_out), .sel(loadIm));
  Multiplexer #(.width(16)) multiplexer_3 (.in0({16{1'b0}}), .in1(ALUdata), .out(multiplexer_3_out), .sel(ALUen));
  Bit_Extender #(.in_width(5), .out_width(4), .\type ("zero")) bit_extender_2 (
    .in(subtractor_1_out), .out(bit_extender_2_out));
  // Probe on multiplexer_1_out
  assign or_1_out = multiplexer_1_out | multiplexer_2_out | {16{1'b0}} | multiplexer_3_out;  // OR_Gate or_1, 16 bits wide
  ALU alu_1 (.A(out1), .B(out2), .OP(bit_extender_2_out), .out_4(out_6));
  Multiplexer #(.width(3)) multiplexer_4 (.in0(3'b000), .in1(out_1[10:8]), .out(multiplexer_4_out), .sel(mv));
  Multiplexer #(.width(3)) multiplexer_5 (.in0(3'b000), .in1(dest), .out(multiplexer_5_out), .sel(mv));
  assign a1 = dest | 3'b000 | multiplexer_4_out | 3'b000;  // OR_Gate or_2, 3 bits wide
  assign a2 = out_1[4:2] | 3'b000 | 3'b000;  // OR_Gate or_3, 3 bits wide
  RAM #(.dataWidth(16), .readbehav("war")) ram_1 ();  // open: addr, we, oe, clk, din, dout
  Multiplexer #(.width(3)) multiplexer_6 (.in0(3'b000), .in1(out_1[10:8]), .out(multiplexer_6_out), .sel(ALUen));
  Multiplexer #(.width(3)) multiplexer_7 (.in0(3'b000), .in1(out_1[10:8]), .out(multiplexer_7_out), .sel(loadIm));
  Register #(.trigger("high"), .width(16)) register_2 (.D(out_6), .en(ALUen), .Q(ALUdata), .clk(clk), .clr(rst));
  assign a = multiplexer_6_out | multiplexer_5_out | multiplexer_7_out;  // OR_Gate or_4, 3 bits wide
  Register #(.trigger("falling"), .width(1)) register_3 (.D(mv), .en(mv), .Q(register_3_q), .clk(clk), .clr(rst));
  Demultiplexer #(.select(3)) demultiplexer_1 (
    .out0(demultiplexer_1_out0), .out1(demultiplexer_1_out1), .out2(demultiplexer_1_out2),
    .out3(demultiplexer_1_out3), .out4(demultiplexer_1_out4), .out5(demultiplexer_1_out5),
    .out6(demultiplexer_1_out6), .out7(demultiplexer_1_out7), .in(or_5_out), .sel(a));
  or or_5 (or_5_out, ALUen, register_3_q, loadIm);
  Demultiplexer #(.select(3), .width(16)) demultiplexer_2 (
    .out0(demultiplexer_2_out0), .out1(demultiplexer_2_out1), .out2(demultiplexer_2_out2),
    .out3(demultiplexer_2_out3), .out4(demultiplexer_2_out4), .out5(demultiplexer_2_out5),
    .out6(demultiplexer_2_out6), .out7(demultiplexer_2_out7), .in(or_1_out), .sel(a));
  Register #(.trigger("high"), .width(16)) R0 (
    .D(demultiplexer_2_out0), .en(demultiplexer_1_out0), .Q(R0_q), .clk(clk), .clr(rst));
  Register #(.trigger("high"), .width(16)) R1 (
    .D(demultiplexer_2_out1), .en(demultiplexer_1_out1), .Q(R1_q), .clk(clk), .clr(rst));
  Register #(.trigger("high"), .width(16)) R2 (
    .D(demultiplexer_2_out2), .en(demultiplexer_1_out2), .Q(R2_q), .clk(clk), .clr(rst));
  Register #(.trigger("high"), .width(16)) R3 (
    .D(demultiplexer_2_out3), .en(demultiplexer_1_out3), .Q(R3_q), .clk(clk), .clr(rst));
  Register #(.trigger("high"), .width(16)) R4 (
    .D(demultiplexer_2_out4), .en(demultiplexer_1_out4), .Q(R4_q), .clk(clk), .clr(rst));
  Register #(.trigger("high"), .width(16)) R5 (
    .D(demultiplexer_2_out5), .en(demultiplexer_1_out5), .Q(R5_q), .clk(clk), .clr(rst));
  Register #(.trigger("high"), .width(16)) R6 (
    .D(demultiplexer_2_out6), .en(demultiplexer_1_out6), .Q(R6_q), .clk(clk), .clr(rst));
  Register #(.trigger("high"), .width(16)) R7 (
    .D(demultiplexer_2_out7), .en(demultiplexer_1_out7), .Q(R7_q), .clk(clk), .clr(rst));
  Multiplexer #(.select(3), .width(16)) multiplexer_8 (
    .in0(R0_q), .in1(R1_q), .in2(R2_q), .in3(R3_q), .in4(R4_q), .in5(R5_q), .in6(R6_q), .in7(R7_q),
    .out(out1), .sel(a1));
  Multiplexer #(.select(3), .width(16)) multiplexer_9 (
    .in0(R0_q), .in1(R1_q), .in2(R2_q), .in3(R3_q), .in4(R4_q), .in5(R5_q), .in6(R6_q), .in7(R7_q),
    .out(out2), .sel(a2));

  assign out_1[7:5] = dest;
  assign out_2 = out_1[15:11];
  assign out_3 = {out_1[10:8], dest, out_1[4:0]};
  assign src = out_1[10:8];

  // Other names for the same wires on the sheet: instr[15:0] = {out_1[15:8], dest, out_1[4:0]};
  //   oper[10:0] = {out_1[10:8], dest, out_1[4:0]}; RB[2:0] = out_1[4:2]; mvdest[2:0] = dest; RA[2:0] = dest;
  //   imReg[2:0] = out_1[10:8]; mvsrc[2:0] = out_1[10:8]; RC[2:0] = out_1[10:8]; opc[4:0] = out_1[15:11]

  // Notes on the sheet:
  //   li
  //   contents of rom_1 (hex, n*v repeats v):
  //   0 9202 9a60
  //   mv
  //   RAM-ze shesaertebelia ramData
endmodule
